# Fritzing sketch esp32_pn532 (saved by Fritzing 0.9.9b)

parts:
  U1 = LuaNode32 / ESP32
  Part1 = PN532 Elechouse RFID NFC Module V3

nets:
  N1: U1.D27, Part1.RSTO
  3V3: U1.3V3, Part1.VCC
  GND: U1.GND, Part1.GND
  N2: U1.D5, Part1.SS
  N3: U1.D18, Part1.SCK
  N4: U1.D19, Part1.MISO
  N5: U1.D23, Part1.MOSI

custom parts:
  LuaNode32 / ESP32: ESP32 based LuaNode32
  PN532 Elechouse RFID NFC Module V3: NFC is a popular technology in recent years. We often heard this work while smart phone company such as Samsung or HTC introduces their latest high-end phones. Almost all the high-end phone in the market support NFC. Near field communication (NFC) is a set of standards for smart phones and similar devices to establish radio communication with each other by touching them together or bringing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
